# Fritzing sketch Robo_pepev2 (saved by Fritzing 0.9.10b)
perfboards: 3

parts:
  U1 = ESP32S-HiLetgo [part_number=ESP32S-HiLetgo]
  S1 = Pushbutton [package="[THT]"]
  R1 = Resistor [tolerance=±5% power=0.25 resistance=220 package=THT]
  J1 = Piezo Speaker  # not connected
  Part1 = Adafruit MAX98357A I2S 3W Class D Amplifier [part_number="Adafruit #3006"]
  M1 = Dagu DGServo 9g (Top view) [part_number=RS001B]
  M2 = Dagu DGServo 9g (Top view) [part_number=RS001B]
  U2 = DFR0071 SD Module [package="SIP (Single Inline) [THT]"]
  C3 = Electrolytic Capacitor [capacitance=100µF voltage=35V package="200 mil [THT, electrolytic]"]
  C5 = Capacitor [part_number=100nF package=cap-pth-small2]
  U4 = Voltage Regulator -- 3.3 V -- LM1117
  TP1 = TP4056 [chip_label=TP4056 package="DIP (Dual Inline) [THT]"]
  U6 = LIPO-110mAh [package=lipo-110]
  U7 = SWITCH_SPDT [package=kps-1290]

nets:
  N1: U1.3.3, U1.GPIO35, S1.Pin_3, S1.Pin_4, R1.Pin_0, U2.5V, U7.P
  N2: U1.GPIO25, Part1.DIN
  N3: U1.GPIO26, Part1.LRCLK
  N4: U1.GPIO27, Part1.BCLK
  GND: U1.GND, R1.Pin_1, Part1.GAIN, M1.gnd, M2.gnd, U2.GND
  N5: U1.GPIO5, U2.SS
  N6: U1.GPIO18, U2.SCK
  N7: U1.GPIO19, U2.MISO
  N8: U1.GPIO23, U2.MOSI
  VCC: Part1.VIN, M1.vcc, M2.vcc
  N9: C3.-, C5.1, U4.GND, TP1.pin6
  N10: C3.+, C5.2, U4.IN, TP1.pin3
  N11: U4.OUT, U7.O
  N12: TP1.pin4, U6.+
  N13: TP1.pin5, U6.-

custom parts:
  ESP32S-HiLetgo: HiLetgo ESP-WROOM-32 ESP32 ESP-32S Development Board 2.4GHz Dual-Mode WiFi + Bluetooth Dual Cores Microcontroller The ESP32 integrated with Antenna switches, RF Balun, power amplifiers, low-noise amplifiers, filters, and management modules, and the entire solution occupies the least area of PCB. 2.4 GHz Wi-Fi plus Bluetooth dual-mode chip, with TSMC Ultra-low power consumption 40nm technology,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
  Adafruit MAX98357A I2S 3W Class D Amplifier: Listen to this good news - we now have an all in one digital audio amp breakout board that works incredibly well with the Raspberry Pi! If you're looking for an easy and low cost way to get you digital sound files bumpin' then the MAX08357 I2S Amp Breakout is for you. It takes standard I2S digital audio input and, not only decodes it into analog, but also amplifies it directly into a speaker.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
  DFR0071 SD Module: The DFRobot SD Card Shield is a simple solution for transferring data to and from a standard SD card. The pinout is directly compatible with Arduino, but can also be used with other microcontrollers. It allows you to add mass storage and data logging to your project.
  Voltage Regulator -- 3.3 V -- LM1117: LM1117-3.3 Voltage regulator, 3.3 V output. Note that the pinout order is not the same as LM7805 or LM7833.
  TP4056: A DIP stand-in part for whatever IC you want. With 6 pins on a 300mil dual inline package (DIP) footprint.
